# Fritzing sketch Buzzer_Led (saved by Fritzing 0.9.3b)
breadboards: 1

parts:
  元件1 = Arduino Uno (Rev3) - ICSP
  LED1 = smd LED [color="Red (633nm)" package="1206 [SMD]"]
  LED2 = smd LED [color="Red (633nm)" package="1206 [SMD]"]
  LED3 = smd LED [color="Red (633nm)" package="1206 [SMD]"]
  LED4 = smd LED [color="Red (633nm)" package="1206 [SMD]"]
  J1 = Piezo Speaker
  LED9 = smd LED [color="Yellow (595nm)" package="1206 [SMD]"]
  LED10 = smd LED [color="Yellow (595nm)" package="1206 [SMD]"]
  LED11 = smd LED [color="Yellow (595nm)" package="1206 [SMD]"]
  LED12 = smd LED [color="Yellow (595nm)" package="1206 [SMD]"]
  S1 = Momentary Switch [package=ksa_sealed_tac_switch]
  元件2 = Bluetooth HC-05 Macho
  U1 = Vibration Motor- ROB-08449 [package=vibe-motor-10mm]

nets:
  5V: 元件1.5V, 元件2.VCC
  N1: 元件1.D8, J1.pin2
  N2: 元件1.D9_PWM, LED1.anode, LED2.anode, LED3.anode, LED4.anode
  N3: 元件1.D10_PWM/SS, LED9.anode, LED10.anode, LED11.anode, LED12.anode
  N4: 元件1.D11_PWM/MOSI, U1.-
  N5: 元件1.D2, 元件2.TXD
  N6: 元件1.D3_PWM, 元件2.RXD
  N7: 元件1.D4, 元件2.State
  N8: 元件1.D7, S1.1
  GND: 元件1.GND, LED1.cathode, LED2.cathode, LED3.cathode, LED4.cathode, J1.pin1, LED9.cathode, LED10.cathode, LED11.cathode, LED12.cathode, S1.3, 元件2.GND, U1.+
